// Digital circuit SOP.dig as structural Verilog
module SOP (
  input  A,
  input  B,
  input  C,
  input  D,
  output Y
);

  wire and_1_out, and_2_out, not_1_out, not_2_out, not_3_out, not_4_out;

  not not_1 (not_1_out, A);
  not not_2 (not_2_out, B);
  not not_3 (not_3_out, C);
  not not_4 (not_4_out, D);
  and and_1 (and_1_out, not_1_out, D);
  and and_2 (and_2_out, A, not_4_out);
  or or_1 (Y, and_1_out, and_2_out);

  // Notes on the sheet:
  //   A: MSB
  //   D: LSB
  //   Use A as the most-significant bit and 
  //   D as the least-significant bit.
endmodule

/* Test case 31DayMonth:
A B C D Y
0 0 0 0 X
0 0 0 1 1
0 0 1 0 0
0 0 1 1 1
0 1 0 0 0
0 1 0 1 1
0 1 1 0 0
0 1 1 1 1
1 0 0 0 1
1 0 0 1 0
1 0 1 0 1
1 0 1 1 0
1 1 0 0 1
1 1 0 1 X
1 1 1 0 X
1 1 1 1 X
*/
